// Logisim project ALU_8_Bit.circ as structural Verilog: 2 circuits, main circuit main
module main (
  input  CLK,
  input  D,
  output Q,
  output not_Q
);

  D_Flipflop d_flipflop_1 (.CLK(CLK), .D(D), .Q(Q), .not_Q(not_Q));
endmodule

module D_Flipflop (
  input  CLK,
  input  D,
  output Q,
  output not_Q
);

  wire nand_1_out, nand_2_out, nand_3_out, nand_4_out, nand_5_out, nand_6_out, not_1_out, not_2_out,
       not_3_out;

  not not_1 (not_1_out, CLK);
  not not_2 (not_2_out, D);
  not not_3 (not_3_out, CLK);
  nand nand_1 (nand_1_out, D, not_1_out);
  nand nand_2 (nand_2_out, not_2_out, not_3_out);
  nand nand_3 (nand_3_out, nand_1_out, nand_4_out);
  nand nand_4 (nand_4_out, nand_3_out, nand_2_out);
  nand nand_5 (nand_5_out, nand_3_out, CLK);
  nand nand_6 (nand_6_out, CLK, nand_4_out);
  nand nand_7 (Q, nand_5_out, not_Q);
  nand nand_8 (not_Q, Q, nand_6_out);

  // Notes on the sheet:
  //   M1
  //   M2
  //   Master_Q
  //   Master_Q_negiert
  //   S1
  //   S2
  //   Slave_Q
  //   Slave_Q_negiert
endmodule
